# Fritzing sketch Mail~Time (saved by Fritzing 0.9.3b)
breadboards: 1

parts:
  Part1 = Arduino Uno (Rev3)
  LD1 = LD
  Part2 = KY-018 Photoresistor Module [package="Breakout board"]
  LED1 = LED - 5mm [color="Red (633nm)" package="5 mm [THT]"]
  R1 = Resistor [tolerance=±5% resistance=260 package=THT]
  T1 = Tactile module - capacitive touchpad [package=THT]

nets:
  N1: Part1.A2, Part2.S
  N2: Part1.D13/SCK, T1.Sig
  N3: Part1.D2, LD1.anode, Part2.-
  N4: Part1.D7, R1.Pin_1
  5V: Part1.5V, T1.VCC
  GND: Part1.GND, LD1.cathode, Part2.Vin, LED1.cathode, T1.GND
  N5: LED1.anode, R1.Pin_0

custom parts:
  LD: A Generic Red Dot Laser Diode Module (~5mW)
  KY-018 Photoresistor Module: KY-018 Photoresistor module, used to measure light intensity. It can determine the presence or absence of light.
  Tactile module - capacitive touchpad: Capacitive touchpad
